// Logisim project 8BitComp.circ as structural Verilog: 14 circuits, main circuit main
module RegisterThing (
  input  [7:0] BUS_IN,
  input  CLOCK,
  input  LOAD_EN,
  input  BUS_OUT_EN,
  output [7:0] BUS_OUT,
  output [7:0] DATA
);

  Register register_1 (.D(BUS_IN), .en(LOAD_EN), .clk(CLOCK), .Q(DATA));  // open: clr
  assign BUS_OUT = BUS_OUT_EN ? DATA : 8'bz;  // Controlled_Buffer controlled_buffer_1
endmodule

module main (
  input  HALT,
  input  in_2,
  input  CLOCK_MODE,
  input  CLOCK_BUTTON,
  input  [7:0] in_5
);

  wire ALU_INPUT_MOD, ALU_INVERT_OUT, ALU_REPLACE_B, and_1_out, clock_1_out, clock_2_out, clock_3_out,
       clock_4_out, clock_5_out, clock_6_out, clock_7_out, comparator_1_eq, comparator_1_gt, DATA_OUT_DIS,
       decoder_1_out0, decoder_1_out1, INST_NOT_DONE, JUMP_DIS, nALU_B_SEL_SYS, nand_3_out, nand_4_out,
       nCLOCK, nDISPLAY_INIT, nDISPLAY_SHOW, nJUMP_COND, nJUMP_INST, nor_1_out, nor_2_out, nor_3_out,
       nor_4_out, nor_5_out, nor_6_out, nor_7_out, nor_8_out, nor_9_out, nor_10_out, nor_11_out, nor_13_out,
       nor_14_out, nor_15_out, nor_16_out, not_1_out, not_2_out, not_3_out, not_6_out, not_7_out, not_8_out,
       not_11_out, not_12_out, not_13_out, not_14_out, not_15_out, not_16_out, not_17_out, not_18_out,
       not_19_out, not_20_out, not_21_out, not_22_out, not_23_out, not_24_out, not_25_out, nRAM_OD,
       PC_OUT_DIS, RAM_ADDR_FROM_DATA, RAM_IN_DIS, RAM_OD, RAM_OUT_DIS, RAM_RW, REG_IN_DIS, REG_OUT_DIS,
       RegisterLoadSelector_out_0, RegisterLoadSelector_out_1, RegisterLoadSelector_out_2,
       RegisterLoadSelector_out_3, RegisterLoadSelector_out_4, registerselector_1_out_0,
       registerselector_1_out_1, registerselector_1_out_2, registerselector_1_out_3,
       registerselector_1_out_4, registerselector_2_out_0, registerselector_2_out_1,
       registerselector_2_out_2, registerselector_2_out_3, USER_INPUT_DIS;
  wire [1:0] ALU_B_SEL, ALU_SELECT;
  wire [2:0] DATA_ROM_data, DATA_ROM_data_2, IO_ROM_data, IO_ROM_data_2, REG_OUT_SEL, SET_REG_SEL;
  wire [3:0] microcodecounter_1_address;
  wire [6:0] ALUOutRegister_data_out;
  wire [7:0] adder_1_out, ADDR_REG, bit_extender_1_out, bit_extender_2_out, bit_extender_3_out,
       bit_extender_4_out, bit_extender_5_out, bit_extender_6_out, controlled_buffer_5_out, decoder_2_out0,
       decoder_3_out0, displaydecoder_1_out_0, displaydecoder_1_out_1, displaydecoder_1_out_2,
       displaydecoder_1_out_3, displaydecoder_1_out_4, displaydecoder_1_out_5, displaydecoder_1_out_6,
       displaydecoder_1_out_7, multiplexer_1_out, multiplexer_4_out, multiplexer_5_out, multiplexer_6_out,
       nand_5_out, not_9_out, not_10_out, OPCODE_ROM_data, programcounter_1_address, ram_1_data,
       RealPC_data_out, Reg0_data_out, Reg1_data_out, Reg2_data_out, Reg3_data_out,
       shiftregister_1_parallel_out, xor_1_out, xor_2_out, xor_3_out, xor_4_out, xor_5_out;

  not not_1 (not_1_out, INST_NOT_DONE);
  ROM OPCODE_ROM (.addr(RealPC_data_out), .data(OPCODE_ROM_data));
  Clock clock_1 (.out(clock_1_out));
  Decoder #(.enable("false")) decoder_1 (.out0(decoder_1_out0), .out1(decoder_1_out1), .sel(CLOCK_MODE));
  nor nor_1 (nor_1_out, nDISPLAY_SHOW, nDISPLAY_SHOW);
  nor nor_2 (nor_2_out, nDISPLAY_INIT, nDISPLAY_INIT);
  nor nor_3 (nor_3_out, clock_1_out, nor_6_out);
  nor nor_4 (nor_4_out, nor_9_out, nor_3_out);
  nor nor_5 (nor_5_out, nor_6_out, decoder_1_out1);
  nor nor_6 (nor_6_out, nor_5_out, decoder_1_out0);
  LedBar #(.matrixcols(4)) ledbar_1 (
    .led0(microcodecounter_1_address[3]), .led1(microcodecounter_1_address[2]),
    .led2(microcodecounter_1_address[1]), .led3(microcodecounter_1_address[0]));
  Clock clock_2 (.out(clock_2_out));
  nor nor_7 (nor_7_out, nor_1_out, nor_2_out);
  nor nor_8 (nor_8_out, nor_4_out, nor_4_out);
  nor nor_9 (nor_9_out, nor_5_out, CLOCK_BUTTON);
  ROM #(.addrWidth(11)) IO_ROM (
    .addr({OPCODE_ROM_data[6:0], microcodecounter_1_address}),
    .data({REG_IN_DIS, IO_ROM_data_2, REG_OUT_DIS, IO_ROM_data}));
  MicrocodeCounter microcodecounter_1 (
    .CLOCK(nCLOCK), .SYNC_RESET_DIS(INST_NOT_DONE), .ASYNC_RESET_DIS(in_2), .COUNT_EN(INST_NOT_DONE),
    .ADDRESS(microcodecounter_1_address));
  not not_2 (not_2_out, nJUMP_INST);
  not not_3 (not_3_out, nJUMP_COND);
  not not_4 (nCLOCK, clock_2_out);
  not not_5 (RAM_OD, nRAM_OD);
  Multiplexer #(.width(8)) multiplexer_1 (
    .in0(ADDR_REG), .in1({DATA_ROM_data_2, ALU_B_SEL, DATA_ROM_data}), .out(multiplexer_1_out),
    .sel(RAM_ADDR_FROM_DATA));
  not not_6 (not_6_out, RAM_RW);
  and and_1 (and_1_out, in_2, ~RAM_OD);  // AND_Gate
  nor nor_10 (nor_10_out, nor_7_out, nCLOCK);
  nor nor_11 (nor_11_out, nor_8_out, HALT);
  nor nor_12 (nRAM_OD, clock_4_out, RAM_OUT_DIS);
  LedBar OPCODE (
    .led0(OPCODE_ROM_data[7]), .led1(OPCODE_ROM_data[6]), .led2(OPCODE_ROM_data[5]),
    .led3(OPCODE_ROM_data[4]), .led4(OPCODE_ROM_data[3]), .led5(OPCODE_ROM_data[2]),
    .led6(OPCODE_ROM_data[1]), .led7(OPCODE_ROM_data[0]));
  nand nand_1 (JUMP_DIS, not_2_out, not_3_out);
  not not_7 (not_7_out, RAM_IN_DIS);
  Clock clock_3 (.out(clock_3_out));
  not not_8 (not_8_out, in_2);
  RAM #(.clearpin("true"), .databus("bidir"), .enables("line"), .trigger("high")) ram_1 (
    .addr(multiplexer_1_out), .we(not_6_out), .oe(and_1_out), .clk(in_2), .data(ram_1_data), .clr(not_8_out));
  Clock clock_4 (.out(clock_4_out));
  nand nand_2 (RAM_RW, not_7_out, clock_3_out);
  ROM #(.addrWidth(11)) ALU_ROM (
    .addr({OPCODE_ROM_data[6:0], microcodecounter_1_address}),
    .data({INST_NOT_DONE, RAM_ADDR_FROM_DATA, nALU_B_SEL_SYS, ALU_INPUT_MOD, ALU_INVERT_OUT, ALU_REPLACE_B, ALU_SELECT}));
  ShiftRegister shiftregister_1 (
    .OUTPUT_DIS(nDISPLAY_SHOW), .RESET_DIS(in_2), .SR_CLOCK(nor_10_out), .R_CLOCK(nor_10_out),
    .SERIAL_IN(nor_2_out), .PARALLEL_OUT(shiftregister_1_parallel_out));  // open: SERIAL_OUT
  Clock clock_5 (.out(clock_5_out));
  LedBar ACTIVE_PC (
    .led0(RealPC_data_out[7]), .led1(RealPC_data_out[6]), .led2(RealPC_data_out[5]),
    .led3(RealPC_data_out[4]), .led4(RealPC_data_out[3]), .led5(RealPC_data_out[2]),
    .led6(RealPC_data_out[1]), .led7(RealPC_data_out[0]));
  RRegister RealPC (
    .LOAD_CLOCK(nCLOCK), .DATA_IN(programcounter_1_address), .RESET_DIS(in_2), .DATA_OUT(RealPC_data_out));
  ROM DATA_ROM (.addr(RealPC_data_out), .data({DATA_ROM_data_2, ALU_B_SEL, DATA_ROM_data}));
  LedBar ledbar_2 (
    .led0(ram_1_data[7]), .led1(ram_1_data[6]), .led2(ram_1_data[5]), .led3(ram_1_data[4]),
    .led4(ram_1_data[3]), .led5(ram_1_data[2]), .led6(ram_1_data[1]), .led7(ram_1_data[0]));
  LedBar IO_FLAGS (
    .led0(REG_IN_DIS), .led1(IO_ROM_data_2[2]), .led2(IO_ROM_data_2[1]), .led3(IO_ROM_data_2[0]),
    .led4(REG_OUT_DIS), .led5(IO_ROM_data[2]), .led6(IO_ROM_data[1]), .led7(IO_ROM_data[0]));
  ProgramCounter programcounter_1 (
    .BUS_IN(ram_1_data), .CLOCK(clock_5_out), .RESET_DIS(in_2), .LOAD_DIS(JUMP_DIS), .COUNT_EN(not_1_out),
    .ADDRESS(programcounter_1_address));
  LedBar PC (
    .led0(programcounter_1_address[7]), .led1(programcounter_1_address[6]),
    .led2(programcounter_1_address[5]), .led3(programcounter_1_address[4]),
    .led4(programcounter_1_address[3]), .led5(programcounter_1_address[2]),
    .led6(programcounter_1_address[1]), .led7(programcounter_1_address[0]));
  Decoder #(.select(3)) decoder_2 (
    .out0(decoder_2_out0[0]), .out1(decoder_2_out0[1]), .out2(decoder_2_out0[2]), .out3(decoder_2_out0[3]),
    .out4(decoder_2_out0[4]), .out5(decoder_2_out0[5]), .out6(decoder_2_out0[6]), .out7(decoder_2_out0[7]),
    .sel(IO_ROM_data), .en(REG_OUT_DIS));
  Decoder #(.select(3)) decoder_3 (
    .out0(decoder_3_out0[0]), .out1(decoder_3_out0[1]), .out2(decoder_3_out0[2]), .out3(decoder_3_out0[3]),
    .out4(decoder_3_out0[4]), .out5(decoder_3_out0[5]), .out6(decoder_3_out0[6]), .out7(decoder_3_out0[7]),
    .sel(IO_ROM_data_2), .en(REG_IN_DIS));
  DisplayDecoder displaydecoder_1 (
    .ROWS(shiftregister_1_parallel_out), .COLUMN(ram_1_data), .OUT_0(displaydecoder_1_out_0),
    .OUT_1(displaydecoder_1_out_1), .OUT_2(displaydecoder_1_out_2), .OUT_3(displaydecoder_1_out_3),
    .OUT_4(displaydecoder_1_out_4), .OUT_5(displaydecoder_1_out_5), .OUT_6(displaydecoder_1_out_6),
    .OUT_7(displaydecoder_1_out_7));
  assign {not_9_out[7:5], USER_INPUT_DIS, RAM_OUT_DIS, PC_OUT_DIS, DATA_OUT_DIS, not_9_out[0]} = ~decoder_2_out0;  // NOT_Gate not_9, 8 bits wide
  nand nand_3 (nand_3_out, IO_ROM_data[1], IO_ROM_data[2]);
  assign {not_10_out[7:6], nDISPLAY_SHOW, nDISPLAY_INIT, RAM_IN_DIS, nJUMP_INST, not_10_out[1:0]} = ~decoder_3_out0;  // NOT_Gate not_10, 8 bits wide
  DotMatrix #(.inputtype("row"), .matrixcols(8), .matrixrows(8)) dotmatrix_1 (
    .row0(displaydecoder_1_out_0), .row1(displaydecoder_1_out_1), .row2(displaydecoder_1_out_2),
    .row3(displaydecoder_1_out_3), .row4(displaydecoder_1_out_4), .row5(displaydecoder_1_out_5),
    .row6(displaydecoder_1_out_6), .row7(displaydecoder_1_out_7));
  LedBar DATA (
    .led0(DATA_ROM_data_2[2]), .led1(DATA_ROM_data_2[1]), .led2(DATA_ROM_data_2[0]), .led3(ALU_B_SEL[1]),
    .led4(ALU_B_SEL[0]), .led5(DATA_ROM_data[2]), .led6(DATA_ROM_data[1]), .led7(DATA_ROM_data[0]));
  LedBar #(.matrixcols(3)) ledbar_3 (.led0(REG_OUT_SEL[2]), .led1(REG_OUT_SEL[1]), .led2(REG_OUT_SEL[0]));
  Multiplexer #(.width(3)) multiplexer_2 (.in0(DATA_ROM_data), .in1(IO_ROM_data), .out(REG_OUT_SEL), .sel(nand_3_out));
  nand nand_4 (nand_4_out, IO_ROM_data_2[1], IO_ROM_data_2[2]);
  assign ram_1_data = not_11_out ? programcounter_1_address : 8'bz;  // Controlled_Buffer controlled_buffer_1
  not not_11 (not_11_out, PC_OUT_DIS);
  not not_12 (not_12_out, DATA_OUT_DIS);
  LedBar #(.matrixcols(3)) ledbar_4 (.led0(SET_REG_SEL[2]), .led1(SET_REG_SEL[1]), .led2(SET_REG_SEL[0]));
  Multiplexer #(.width(3)) multiplexer_3 (
    .in0(DATA_ROM_data_2), .in1(IO_ROM_data_2), .out(SET_REG_SEL), .sel(nand_4_out));
  assign ram_1_data = not_12_out ? {DATA_ROM_data_2, ALU_B_SEL, DATA_ROM_data} : 8'bz;  // Controlled_Buffer controlled_buffer_2
  LedBar ledbar_5 (
    .led0(ram_1_data[7]), .led1(ram_1_data[6]), .led2(ram_1_data[5]), .led3(ram_1_data[4]),
    .led4(ram_1_data[3]), .led5(ram_1_data[2]), .led6(ram_1_data[1]), .led7(ram_1_data[0]));
  Pull_Resistor pull_resistor_1 (.node(ram_1_data[7]));
  Pull_Resistor pull_resistor_2 (.node(ram_1_data[6]));
  Pull_Resistor pull_resistor_3 (.node(ram_1_data[5]));
  Pull_Resistor pull_resistor_4 (.node(ram_1_data[4]));
  Pull_Resistor pull_resistor_5 (.node(ram_1_data[3]));
  Pull_Resistor pull_resistor_6 (.node(ram_1_data[2]));
  Pull_Resistor pull_resistor_7 (.node(ram_1_data[1]));
  Pull_Resistor pull_resistor_8 (.node(ram_1_data[0]));
  not not_13 (not_13_out, USER_INPUT_DIS);
  assign ram_1_data = not_13_out ? in_5 : 8'bz;  // Controlled_Buffer controlled_buffer_3
  RRegister Reg0 (
    .LOAD_CLOCK(RegisterLoadSelector_out_0), .DATA_IN({nJUMP_COND, ALUOutRegister_data_out}),
    .RESET_DIS(in_2), .DATA_OUT(Reg0_data_out));
  not not_14 (not_14_out, registerselector_1_out_0);
  assign ram_1_data = not_14_out ? Reg0_data_out : 8'bz;  // Controlled_Buffer controlled_buffer_4
  LedBar ledbar_6 (
    .led0(Reg0_data_out[7]), .led1(Reg0_data_out[6]), .led2(Reg0_data_out[5]), .led3(Reg0_data_out[4]),
    .led4(Reg0_data_out[3]), .led5(Reg0_data_out[2]), .led6(Reg0_data_out[1]), .led7(Reg0_data_out[0]));
  not not_15 (not_15_out, registerselector_2_out_0);
  assign controlled_buffer_5_out = not_15_out ? Reg0_data_out : 8'bz;  // Controlled_Buffer controlled_buffer_5
  LedBar ledbar_7 (
    .led0(controlled_buffer_5_out[7]), .led1(controlled_buffer_5_out[6]), .led2(controlled_buffer_5_out[5]),
    .led3(controlled_buffer_5_out[4]), .led4(controlled_buffer_5_out[3]), .led5(controlled_buffer_5_out[2]),
    .led6(controlled_buffer_5_out[1]), .led7(controlled_buffer_5_out[0]));
  nor nor_13 (nor_13_out, ALU_INPUT_MOD, ALU_INPUT_MOD);
  Multiplexer #(.width(8)) multiplexer_4 (
    .in0(controlled_buffer_5_out), .in1({8{1'b1}}), .out(multiplexer_4_out), .sel(ALU_REPLACE_B));
  nor nor_14 (nor_14_out, ALU_INVERT_OUT, ALU_INVERT_OUT);
  assign bit_extender_1_out = {{7{nor_15_out}}, nor_15_out};  // Bit_Extender bit_extender_1
  nor nor_15 (nor_15_out, nor_13_out, ALU_REPLACE_B);
  assign bit_extender_2_out = {{7{ALU_INPUT_MOD}}, ALU_INPUT_MOD};  // Bit_Extender bit_extender_2
  assign bit_extender_3_out = {{7{nor_16_out}}, nor_16_out};  // Bit_Extender bit_extender_3
  nor nor_16 (nor_16_out, nor_14_out, ALU_INPUT_MOD);
  assign xor_1_out = ram_1_data ^ bit_extender_1_out;  // XOR_Gate xor_1, 8 bits wide
  assign xor_2_out = multiplexer_4_out ^ bit_extender_2_out;  // XOR_Gate xor_2, 8 bits wide
  assign xor_3_out = ram_1_data ^ bit_extender_3_out;  // XOR_Gate xor_3, 8 bits wide
  RRegister Reg1 (
    .LOAD_CLOCK(RegisterLoadSelector_out_1), .DATA_IN({nJUMP_COND, ALUOutRegister_data_out}),
    .RESET_DIS(in_2), .DATA_OUT(Reg1_data_out));
  not not_16 (not_16_out, registerselector_1_out_1);
  assign ram_1_data = not_16_out ? Reg1_data_out : 8'bz;  // Controlled_Buffer controlled_buffer_6
  LedBar ledbar_8 (
    .led0(Reg1_data_out[7]), .led1(Reg1_data_out[6]), .led2(Reg1_data_out[5]), .led3(Reg1_data_out[4]),
    .led4(Reg1_data_out[3]), .led5(Reg1_data_out[2]), .led6(Reg1_data_out[1]), .led7(Reg1_data_out[0]));
  not not_17 (not_17_out, registerselector_2_out_1);
  assign controlled_buffer_5_out = not_17_out ? Reg1_data_out : 8'bz;  // Controlled_Buffer controlled_buffer_7
  not not_18 (not_18_out, comparator_1_gt);
  not not_19 (not_19_out, comparator_1_eq);
  Comparator #(.mode("unsigned")) comparator_1 (
    .a(xor_1_out), .b(xor_2_out), .gt(comparator_1_gt), .eq(comparator_1_eq));  // open: lt
  assign bit_extender_4_out = {{7{not_18_out}}, not_18_out};  // Bit_Extender bit_extender_4
  assign bit_extender_5_out = {{7{not_19_out}}, not_19_out};  // Bit_Extender bit_extender_5
  Adder adder_1 (.a(xor_3_out), .b(xor_2_out), .out(adder_1_out));  // open: cin, cout
  assign xor_4_out = ram_1_data ^ controlled_buffer_5_out;  // XOR_Gate xor_4, 8 bits wide
  Multiplexer #(.width(8)) multiplexer_5 (
    .in0(xor_4_out), .in1({1'b0, ram_1_data[7:1]}), .out(multiplexer_5_out), .sel(ALU_INPUT_MOD));
  LedBar ledbar_9 (
    .led0(adder_1_out[7]), .led1(adder_1_out[6]), .led2(adder_1_out[5]), .led3(adder_1_out[4]),
    .led4(adder_1_out[3]), .led5(adder_1_out[2]), .led6(adder_1_out[1]), .led7(adder_1_out[0]));
  RRegister Reg2 (
    .LOAD_CLOCK(RegisterLoadSelector_out_2), .DATA_IN({nJUMP_COND, ALUOutRegister_data_out}),
    .RESET_DIS(in_2), .DATA_OUT(Reg2_data_out));
  not not_20 (not_20_out, registerselector_1_out_2);
  assign ram_1_data = not_20_out ? Reg2_data_out : 8'bz;  // Controlled_Buffer controlled_buffer_8
  LedBar ledbar_10 (
    .led0(Reg2_data_out[7]), .led1(Reg2_data_out[6]), .led2(Reg2_data_out[5]), .led3(Reg2_data_out[4]),
    .led4(Reg2_data_out[3]), .led5(Reg2_data_out[2]), .led6(Reg2_data_out[1]), .led7(Reg2_data_out[0]));
  not not_21 (not_21_out, registerselector_2_out_2);
  assign controlled_buffer_5_out = not_21_out ? Reg2_data_out : 8'bz;  // Controlled_Buffer controlled_buffer_9
  assign nand_5_out = ~(xor_1_out & xor_2_out);  // NAND_Gate nand_5, 8 bits wide
  Multiplexer #(.select(3), .width(8)) multiplexer_6 (
    .in0(adder_1_out), .in1(bit_extender_4_out), .in2(bit_extender_5_out), .in3(nand_5_out),
    .in4(bit_extender_5_out), .in5(bit_extender_4_out), .in6(adder_1_out), .in7(multiplexer_5_out),
    .out(multiplexer_6_out), .sel({ALU_REPLACE_B, ALU_SELECT}));
  RRegister Reg3 (
    .LOAD_CLOCK(RegisterLoadSelector_out_3), .DATA_IN({nJUMP_COND, ALUOutRegister_data_out}),
    .RESET_DIS(in_2), .DATA_OUT(Reg3_data_out));
  not not_22 (not_22_out, registerselector_1_out_3);
  assign ram_1_data = not_22_out ? Reg3_data_out : 8'bz;  // Controlled_Buffer controlled_buffer_10
  not not_23 (not_23_out, registerselector_2_out_3);
  assign controlled_buffer_5_out = not_23_out ? Reg3_data_out : 8'bz;  // Controlled_Buffer controlled_buffer_11
  LedBar ledbar_11 (
    .led0(Reg3_data_out[7]), .led1(Reg3_data_out[6]), .led2(Reg3_data_out[5]), .led3(Reg3_data_out[4]),
    .led4(Reg3_data_out[3]), .led5(Reg3_data_out[2]), .led6(Reg3_data_out[1]), .led7(Reg3_data_out[0]));
  assign bit_extender_6_out = {{7{ALU_INVERT_OUT}}, ALU_INVERT_OUT};  // Bit_Extender bit_extender_6
  RRegister Reg4 (
    .LOAD_CLOCK(RegisterLoadSelector_out_4), .DATA_IN({nJUMP_COND, ALUOutRegister_data_out}),
    .RESET_DIS(in_2), .DATA_OUT(ADDR_REG));
  not not_24 (not_24_out, registerselector_1_out_4);
  assign ram_1_data = not_24_out ? ADDR_REG : 8'bz;  // Controlled_Buffer controlled_buffer_12
  not not_25 (not_25_out, nALU_B_SEL_SYS);
  assign controlled_buffer_5_out = not_25_out ? ADDR_REG : 8'bz;  // Controlled_Buffer controlled_buffer_13
  LedBar ledbar_12 (
    .led0(xor_5_out[7]), .led1(xor_5_out[6]), .led2(xor_5_out[5]), .led3(xor_5_out[4]), .led4(xor_5_out[3]),
    .led5(xor_5_out[2]), .led6(xor_5_out[1]), .led7(xor_5_out[0]));
  assign xor_5_out = bit_extender_6_out ^ multiplexer_6_out;  // XOR_Gate xor_5, 8 bits wide
  LedBar ledbar_13 (
    .led0(ADDR_REG[7]), .led1(ADDR_REG[6]), .led2(ADDR_REG[5]), .led3(ADDR_REG[4]), .led4(ADDR_REG[3]),
    .led5(ADDR_REG[2]), .led6(ADDR_REG[1]), .led7(ADDR_REG[0]));
  Clock clock_6 (.out(clock_6_out));
  Clock clock_7 (.out(clock_7_out));
  RegisterSelector RegisterLoadSelector (
    .A(SET_REG_SEL[0]), .B(SET_REG_SEL[1]), .C(SET_REG_SEL[2]), .EN_OUT_1(clock_6_out),
    .DIS_OUT_2(REG_IN_DIS), .DIS_OUT_3(1'b0), .OUT_0(RegisterLoadSelector_out_0),
    .OUT_1(RegisterLoadSelector_out_1), .OUT_2(RegisterLoadSelector_out_2),
    .OUT_3(RegisterLoadSelector_out_3), .OUT_4(RegisterLoadSelector_out_4));  // open: OUT_5, OUT_6, OUT_7
  RegisterSelector registerselector_1 (
    .A(REG_OUT_SEL[0]), .B(REG_OUT_SEL[1]), .C(REG_OUT_SEL[2]), .EN_OUT_1(1'b1), .DIS_OUT_2(1'b0),
    .DIS_OUT_3(REG_OUT_DIS), .OUT_0(registerselector_1_out_0), .OUT_1(registerselector_1_out_1),
    .OUT_2(registerselector_1_out_2), .OUT_3(registerselector_1_out_3), .OUT_4(registerselector_1_out_4));  // open: OUT_5, OUT_6, OUT_7
  RegisterSelector registerselector_2 (
    .A(ALU_B_SEL[0]), .B(ALU_B_SEL[1]), .C(1'b0), .EN_OUT_1(nALU_B_SEL_SYS), .DIS_OUT_2(1'b0),
    .DIS_OUT_3(1'b0), .OUT_0(registerselector_2_out_0), .OUT_1(registerselector_2_out_1),
    .OUT_2(registerselector_2_out_2), .OUT_3(registerselector_2_out_3));  // open: OUT_4, OUT_5, OUT_6, OUT_7
  RRegister ALUOutRegister (
    .LOAD_CLOCK(clock_7_out), .DATA_IN(xor_5_out), .RESET_DIS(in_2),
    .DATA_OUT({nJUMP_COND, ALUOutRegister_data_out}));
  LedBar ledbar_14 (
    .led0(nJUMP_COND), .led1(ALUOutRegister_data_out[6]), .led2(ALUOutRegister_data_out[5]),
    .led3(ALUOutRegister_data_out[4]), .led4(ALUOutRegister_data_out[3]), .led5(ALUOutRegister_data_out[2]),
    .led6(ALUOutRegister_data_out[1]), .led7(ALUOutRegister_data_out[0]));

  // Other names for the same wires on the sheet: ALU_SELECT[2] = ALU_REPLACE_B; MASTER_RESET_DIS = in_2

  // Notes on the sheet:
  //   contents of OPCODE_ROM (hex, n*v repeats v):
  //   2 31 1 3c c 42
  //   contents of IO_ROM (hex, n*v repeats v):
  //   16*88 77 15*88 9 15*88 19 15*88 29 15*88 39 31*88 49 0 49 0 12*88 49 11 49 11 12*88 49 22 49 22
  //   12*88 49 33 49 33 92*88 b0 15*88 b1 15*88 b2 15*88 b3 15*88 b 15*88 1b 15*88 2b 15*88 3b 15*88 b7
  //   15*88 b9 15*88 7b 95*88 49 43 b 13*88 49 43 1b 13*88 49 43 2b 29*88 49 43 b0 13*88 49 43 b1 13*88 49
  //   43 b2 29*88 49 40 14*88 49 41 14*88 49 42 94*88 43 b9 33 13*88 43 b7 33 237*88 77 15*88 77 15*88 77
  //   31*88 77 15*88 77 15*88 77 31*88 77 15*88 77 15*88 77 15*88 77 79*88 77 63*88 77 15*88 77 15*88 77
  //   15*88 77 15*88 77 15*88 77 15*88 77 15*88 77 79*88 84 a9 14*88 80 a9 14*88 43 3a b3 34 84 a9 10*88
  //   49 33 43 84 ab 203*88 7c 15*88 d7 15*88 e7 223*88
  //   contents of ALU_ROM (hex, n*v repeats v):
  //   c 15*0 16 15*0 16 15*0 16 15*0 16 15*0 16 31*0 80 80 98 8 12*0 80 80 98 8 12*0 80 80 98 8 12*0 80 80
  //   98 8 92*0 56 15*0 56 15*0 56 15*0 56 15*0 56 15*0 56 15*0 56 15*0 56 15*0 c 15*0 c 15*0 16 95*0 96
  //   80 16 13*0 96 80 16 13*0 96 80 16 29*0 96 80 c 13*0 96 80 c 13*0 96 80 c 29*0 96 15*0 96 15*0 96
  //   95*0 96 8c e 13*0 96 8c e 237*0 2a 15*0 1c 15*0 c 31*0 22 15*0 14 15*0 4 31*0 29 15*0 31 15*0 39
  //   15*0 21 79*0 20 63*0 17 15*0 1e 15*0 2b 15*0 33 15*0 3b 15*0 3b 15*0 27 15*0 2f 79*0 87 c 14*0 96 c
  //   14*0 96 8e 8c 8e 87 c 10*0 96 90 96 87 c 203*0 16 15*0 c 15*0 c 207*0 16*8c
  //   contents of DATA_ROM (hex, n*v repeats v):
  //   1 2 41 62 0 4
endmodule

module ProgramCounter (
  input  [7:0] BUS_IN,
  input  CLOCK,
  input  RESET_DIS,
  input  LOAD_DIS,
  input  COUNT_EN,
  output [7:0] ADDRESS
);

  wire n74161_1_pin15;

  _74161 u_74161_1 (
    .pin1(RESET_DIS), .pin2(CLOCK), .pin3(BUS_IN[0]), .pin4(BUS_IN[1]), .pin5(BUS_IN[2]), .pin6(BUS_IN[3]),
    .pin7(COUNT_EN), .pin15(n74161_1_pin15), .pin14(ADDRESS[0]), .pin13(ADDRESS[1]), .pin12(ADDRESS[2]),
    .pin11(ADDRESS[3]), .pin10(COUNT_EN), .pin9(LOAD_DIS));
  _74161 u_74161_2 (
    .pin1(RESET_DIS), .pin2(CLOCK), .pin3(BUS_IN[4]), .pin4(BUS_IN[5]), .pin5(BUS_IN[6]), .pin6(BUS_IN[7]),
    .pin7(n74161_1_pin15), .pin14(ADDRESS[4]), .pin13(ADDRESS[5]), .pin12(ADDRESS[6]), .pin11(ADDRESS[7]),
    .pin10(n74161_1_pin15), .pin9(LOAD_DIS));  // open: pin15
endmodule

module FlagsMicrocodeROM (
  input  [7:0] OPCODE,
  input  [3:0] MICRO_COUNT,
  output [7:0] BUS_IN_FLAGS,
  output [7:0] BUS_OUT_FLAGS,
  output OUT_0,
  output OUT_1
);

  wire [7:2] rom_1_data;

  ROM #(.addrWidth(11)) rom_1 (.addr({OPCODE[6:0], MICRO_COUNT}), .data({rom_1_data, OUT_1, OUT_0}));
  Decoder #(.select(3)) decoder_1 (
    .out0(BUS_IN_FLAGS[0]), .out1(BUS_IN_FLAGS[1]), .out2(BUS_IN_FLAGS[2]), .out3(BUS_IN_FLAGS[3]),
    .out4(BUS_IN_FLAGS[4]), .out5(BUS_IN_FLAGS[5]), .out6(BUS_IN_FLAGS[6]), .out7(BUS_IN_FLAGS[7]),
    .sel(rom_1_data[7:5]));  // open: en
  Decoder #(.select(3)) decoder_2 (
    .out0(BUS_OUT_FLAGS[0]), .out1(BUS_OUT_FLAGS[1]), .out2(BUS_OUT_FLAGS[2]), .out3(BUS_OUT_FLAGS[3]),
    .out4(BUS_OUT_FLAGS[4]), .out5(BUS_OUT_FLAGS[5]), .out6(BUS_OUT_FLAGS[6]), .out7(BUS_OUT_FLAGS[7]),
    .sel(rom_1_data[4:2]));  // open: en

  // Notes on the sheet:
  //   contents of rom_1 (hex, n*v repeats v):
  //   16*0 2 15*ff 2 15*ff 2 15*ff 2 15*ff 29 29 1966*ff
endmodule

module RAMThing (
  input  [7:0] BUS_IN,
  input  [7:0] ADDRESS,
  input  CLOCK,
  input  LOAD_EN,
  input  OUTPUT_EN,
  output [7:0] BUS_OUT
);
endmodule

module MicrocodeCounter (
  input  CLOCK,
  input  SYNC_RESET_DIS,
  input  ASYNC_RESET_DIS,
  input  COUNT_EN,
  output [3:0] ADDRESS
);

  wire n74161_1_pin3;

  _74161 u_74161_1 (
    .pin1(ASYNC_RESET_DIS), .pin2(CLOCK), .pin3(n74161_1_pin3), .pin4(n74161_1_pin3), .pin5(n74161_1_pin3),
    .pin6(n74161_1_pin3), .pin7(COUNT_EN), .pin14(ADDRESS[0]), .pin13(ADDRESS[1]), .pin12(ADDRESS[2]),
    .pin11(ADDRESS[3]), .pin10(COUNT_EN), .pin9(SYNC_RESET_DIS));  // open: pin15
  // also tied to GND on the sheet: n74161_1_pin3
endmodule

module PlusOne (
  input  [7:0] VAL_IN,
  input  OUTPUT_EN,
  output [7:0] VAL_OUT
);

  wire [7:0] adder_1_out;

  Adder adder_1 (.a(VAL_IN), .b(8'h1), .out(adder_1_out));  // open: cin, cout
  assign VAL_OUT = OUTPUT_EN ? adder_1_out : 8'bz;  // Controlled_Buffer controlled_buffer_1
endmodule

module RLRegister (
  input  CLOCK,
  input  [7:0] DATA_IN,
  input  LOAD_DIS,
  input  RESET_EN,
  input  OUTPUT_DIS,
  output [7:0] DATA_OUT
);

  wire and_1_out, not_1_out, not_2_out;
  wire [7:0] n74273_1_pin2;

  and and_1 (and_1_out, ~LOAD_DIS, CLOCK);  // AND_Gate
  not not_1 (not_1_out, RESET_EN);
  not not_2 (not_2_out, OUTPUT_DIS);
  _74273 u_74273_1 (
    .pin1(not_1_out), .pin2(n74273_1_pin2[0]), .pin3(DATA_IN[0]), .pin4(DATA_IN[1]), .pin5(n74273_1_pin2[1]),
    .pin6(n74273_1_pin2[2]), .pin7(DATA_IN[2]), .pin8(DATA_IN[3]), .pin9(n74273_1_pin2[3]),
    .pin19(n74273_1_pin2[7]), .pin18(DATA_IN[7]), .pin17(DATA_IN[6]), .pin16(n74273_1_pin2[6]),
    .pin15(n74273_1_pin2[5]), .pin14(DATA_IN[5]), .pin13(DATA_IN[4]), .pin12(n74273_1_pin2[4]),
    .pin11(and_1_out));
  assign DATA_OUT = not_2_out ? n74273_1_pin2 : 8'bz;  // Controlled_Buffer controlled_buffer_1
endmodule

module RRegister (
  input  LOAD_CLOCK,
  input  [7:0] DATA_IN,
  input  RESET_DIS,
  output [7:0] DATA_OUT
);

  _74273 u_74273_1 (
    .pin1(RESET_DIS), .pin2(DATA_OUT[0]), .pin3(DATA_IN[0]), .pin4(DATA_IN[1]), .pin5(DATA_OUT[1]),
    .pin6(DATA_OUT[2]), .pin7(DATA_IN[2]), .pin8(DATA_IN[3]), .pin9(DATA_OUT[3]), .pin19(DATA_OUT[7]),
    .pin18(DATA_IN[7]), .pin17(DATA_IN[6]), .pin16(DATA_OUT[6]), .pin15(DATA_OUT[5]), .pin14(DATA_IN[5]),
    .pin13(DATA_IN[4]), .pin12(DATA_OUT[4]), .pin11(LOAD_CLOCK));
endmodule

module RegisterSelector (
  input  A,
  input  B,
  input  C,
  input  EN_OUT_1,
  input  DIS_OUT_2,
  input  DIS_OUT_3,
  output OUT_0,
  output OUT_1,
  output OUT_2,
  output OUT_3,
  output OUT_4,
  output OUT_5,
  output OUT_6,
  output OUT_7
);

  wire and_1_out;
  wire [7:0] decoder_1_out0;

  and and_1 (and_1_out, EN_OUT_1, ~DIS_OUT_2, ~DIS_OUT_3);  // AND_Gate
  Decoder #(.select(3)) decoder_1 (
    .out0(decoder_1_out0[0]), .out1(decoder_1_out0[1]), .out2(decoder_1_out0[2]), .out3(decoder_1_out0[3]),
    .out4(decoder_1_out0[4]), .out5(decoder_1_out0[5]), .out6(decoder_1_out0[6]), .out7(decoder_1_out0[7]),
    .sel({C, B, A}), .en(and_1_out));
  assign {OUT_7, OUT_6, OUT_5, OUT_4, OUT_3, OUT_2, OUT_1, OUT_0} = ~decoder_1_out0;  // NOT_Gate not_1, 8 bits wide
endmodule

module ALUROM (
  input  [7:0] OPCODE,
  input  [3:0] MICRO_COUNT,
  output [7:0] DATA
);

  ROM #(.addrWidth(11)) rom_1 (.addr({OPCODE[6:0], MICRO_COUNT}), .data(DATA));

  // Notes on the sheet:
  //   contents of rom_1 (hex, n*v repeats v):
  //   16*0 7a 15*ff 2 15*ff 2 15*ff 2 15*ff 29 29 1966*ff
endmodule

module MicrocodeROM (
  input  [7:0] OPCODE,
  input  [3:0] MICRO_COUNT,
  output [7:0] IO_FLAGS,
  output [7:0] ALU_FLAGS
);

  ROM #(.addrWidth(11)) rom_1 (.addr({OPCODE[6:0], MICRO_COUNT}), .data(IO_FLAGS));
  ROM #(.addrWidth(11)) rom_2 (.addr({OPCODE[6:0], MICRO_COUNT}), .data(ALU_FLAGS));

  // Notes on the sheet:
  //   contents of rom_1 (hex, n*v repeats v):
  //   16*0 77 175*ff 77 15*ff 77 559*ff 9 15*ff 19 15*ff 29 15*ff 39 143*ff 77 63*ff 44 a9 30*ff a9 991*ff
  //   contents of rom_2 (hex, n*v repeats v):
  //   7*80 0 8*80 60 175*ff e 15*ff 6 559*ff 76 15*ff 76 15*ff 76 15*ff 76 143*ff 76 63*ff 87 40 30*ff 40
  //   991*ff
endmodule

module ShiftRegister (
  input  OUTPUT_DIS,
  input  RESET_DIS,
  input  SR_CLOCK,
  input  R_CLOCK,
  input  SERIAL_IN,
  output [7:0] PARALLEL_OUT,
  output SERIAL_OUT
);

  wire d_ff_1_q, d_ff_3_q, d_ff_5_q, d_ff_7_q, d_ff_9_q, d_ff_11_q, d_ff_13_q, not_1_out, not_2_out;
  wire [7:0] d_ff_2_q;

  not not_1 (not_1_out, OUTPUT_DIS);
  D_Flip_Flop d_ff_1 (.D(SERIAL_IN), .clk(SR_CLOCK), .Q(d_ff_1_q), .reset(not_2_out));  // open: Qn, preset
  not not_2 (not_2_out, RESET_DIS);
  D_Flip_Flop d_ff_2 (.D(d_ff_1_q), .clk(R_CLOCK), .Q(d_ff_2_q[0]));  // open: Qn, preset, reset
  D_Flip_Flop d_ff_3 (.D(d_ff_1_q), .clk(SR_CLOCK), .Q(d_ff_3_q), .reset(not_2_out));  // open: Qn, preset
  D_Flip_Flop d_ff_4 (.D(d_ff_3_q), .clk(R_CLOCK), .Q(d_ff_2_q[1]));  // open: Qn, preset, reset
  D_Flip_Flop d_ff_5 (.D(d_ff_3_q), .clk(SR_CLOCK), .Q(d_ff_5_q), .reset(not_2_out));  // open: Qn, preset
  D_Flip_Flop d_ff_6 (.D(d_ff_5_q), .clk(R_CLOCK), .Q(d_ff_2_q[2]));  // open: Qn, preset, reset
  D_Flip_Flop d_ff_7 (.D(d_ff_5_q), .clk(SR_CLOCK), .Q(d_ff_7_q), .reset(not_2_out));  // open: Qn, preset
  D_Flip_Flop d_ff_8 (.D(d_ff_7_q), .clk(R_CLOCK), .Q(d_ff_2_q[3]));  // open: Qn, preset, reset
  D_Flip_Flop d_ff_9 (.D(d_ff_7_q), .clk(SR_CLOCK), .Q(d_ff_9_q), .reset(not_2_out));  // open: Qn, preset
  D_Flip_Flop d_ff_10 (.D(d_ff_9_q), .clk(R_CLOCK), .Q(d_ff_2_q[4]));  // open: Qn, preset, reset
  D_Flip_Flop d_ff_11 (.D(d_ff_9_q), .clk(SR_CLOCK), .Q(d_ff_11_q), .reset(not_2_out));  // open: Qn, preset
  D_Flip_Flop d_ff_12 (.D(d_ff_11_q), .clk(R_CLOCK), .Q(d_ff_2_q[5]));  // open: Qn, preset, reset
  D_Flip_Flop d_ff_13 (.D(d_ff_11_q), .clk(SR_CLOCK), .Q(d_ff_13_q), .reset(not_2_out));  // open: Qn, preset
  D_Flip_Flop d_ff_14 (.D(d_ff_13_q), .clk(R_CLOCK), .Q(d_ff_2_q[6]));  // open: Qn, preset, reset
  D_Flip_Flop d_ff_15 (.D(d_ff_13_q), .clk(SR_CLOCK), .Q(SERIAL_OUT), .reset(not_2_out));  // open: Qn, preset
  D_Flip_Flop d_ff_16 (.D(SERIAL_OUT), .clk(R_CLOCK), .Q(d_ff_2_q[7]));  // open: Qn, preset, reset
  assign PARALLEL_OUT = not_1_out ? d_ff_2_q : 8'bz;  // Controlled_Buffer controlled_buffer_1
endmodule

module DisplayDecoder (
  input  [7:0] ROWS,
  input  [7:0] COLUMN,
  output [7:0] OUT_0,
  output [7:0] OUT_1,
  output [7:0] OUT_2,
  output [7:0] OUT_3,
  output [7:0] OUT_4,
  output [7:0] OUT_5,
  output [7:0] OUT_6,
  output [7:0] OUT_7
);

  wire [7:0] bit_extender_1_out, bit_extender_2_out, bit_extender_3_out, bit_extender_4_out,
       bit_extender_5_out, bit_extender_6_out, bit_extender_7_out, bit_extender_8_out;

  assign bit_extender_1_out = {{7{COLUMN[0]}}, COLUMN[0]};  // Bit_Extender bit_extender_1
  assign bit_extender_2_out = {{7{COLUMN[1]}}, COLUMN[1]};  // Bit_Extender bit_extender_2
  assign bit_extender_3_out = {{7{COLUMN[2]}}, COLUMN[2]};  // Bit_Extender bit_extender_3
  assign bit_extender_4_out = {{7{COLUMN[3]}}, COLUMN[3]};  // Bit_Extender bit_extender_4
  assign bit_extender_5_out = {{7{COLUMN[4]}}, COLUMN[4]};  // Bit_Extender bit_extender_5
  assign bit_extender_6_out = {{7{COLUMN[5]}}, COLUMN[5]};  // Bit_Extender bit_extender_6
  assign bit_extender_7_out = {{7{COLUMN[6]}}, COLUMN[6]};  // Bit_Extender bit_extender_7
  assign bit_extender_8_out = {{7{COLUMN[7]}}, COLUMN[7]};  // Bit_Extender bit_extender_8
  assign OUT_0 = bit_extender_1_out & ROWS;  // AND_Gate and_1, 8 bits wide
  assign OUT_1 = bit_extender_2_out & ROWS;  // AND_Gate and_2, 8 bits wide
  assign OUT_2 = bit_extender_3_out & ROWS;  // AND_Gate and_3, 8 bits wide
  assign OUT_3 = bit_extender_4_out & ROWS;  // AND_Gate and_4, 8 bits wide
  assign OUT_4 = bit_extender_5_out & ROWS;  // AND_Gate and_5, 8 bits wide
  assign OUT_5 = bit_extender_6_out & ROWS;  // AND_Gate and_6, 8 bits wide
  assign OUT_6 = bit_extender_7_out & ROWS;  // AND_Gate and_7, 8 bits wide
  assign OUT_7 = bit_extender_8_out & ROWS;  // AND_Gate and_8, 8 bits wide
endmodule
